// Logisim project 7 segment display.circ as structural Verilog: 1 circuit, main circuit main
module main (
);

  wire clock_1_out, not_1_out;

  Clock clock_1 (.out(clock_1_out));
  _7_Segment_Display u_7_segment_display_1 (
    .g(not_1_out), .f(not_1_out), .a(not_1_out), .b(not_1_out), .e(not_1_out), .d(not_1_out), .c(not_1_out),
    .dp(not_1_out));
  not not_1 (not_1_out, clock_1_out);
endmodule
