// Logisim project Assignment.circ as structural Verilog: 1 circuit, main circuit main
module main (
  input  A,
  input  B,
  input  C,
  input  D,
  output F1,
  output F2
);

  wire not_1_out, not_2_out, not_3_out, T1_out, T2_out, T3_out, T4_out;

  not not_1 (not_1_out, B);
  not not_2 (not_2_out, A);
  or T3 (T3_out, A, T1_out);
  and T1 (T1_out, not_1_out, C);
  and T2 (T2_out, not_2_out, B);
  xor T4 (T4_out, T2_out, D);
  or or_1 (F2, T2_out, not_3_out);
  not not_3 (not_3_out, D);
  or or_2 (F1, T3_out, T4_out);
endmodule
