// Logisim project Asyn_Up.circ as structural Verilog: 1 circuit, main circuit main
module main (
  input  in_1,
  output out_2,
  output out_3,
  output out_4,
  output out_5
);

  wire clock_1_out, j_k_ff_2_q, j_k_ff_3_q, j_k_ff_4_q;

  J_K_Flip_Flop j_k_ff_1 (.J(in_1), .clk(j_k_ff_2_q), .K(in_1), .Qn(out_2), .en(in_1));  // open: Q, preset, reset
  J_K_Flip_Flop j_k_ff_2 (
    .J(in_1), .clk(j_k_ff_3_q), .K(in_1), .Q(j_k_ff_2_q), .Qn(out_3), .en(in_1));  // open: preset, reset
  Clock clock_1 (.out(clock_1_out));
  J_K_Flip_Flop j_k_ff_3 (
    .J(in_1), .clk(j_k_ff_4_q), .K(in_1), .Q(j_k_ff_3_q), .Qn(out_4), .en(in_1));  // open: preset, reset
  J_K_Flip_Flop j_k_ff_4 (
    .J(in_1), .clk(clock_1_out), .K(in_1), .Q(j_k_ff_4_q), .Qn(out_5), .en(in_1));  // open: preset, reset

  // Notes on the sheet:
  //   Asychronous Up Counter
endmodule
