// Logisim project Asynchronous.circ as structural Verilog: 1 circuit, main circuit main
module main (
  input  in_1,
  input  in_2,
  output out_3,
  output out_4,
  output out_5,
  output out_6
);

  wire clock_1_out, j_k_ff_1_qn, j_k_ff_2_qn, j_k_ff_3_qn, not_1_out;

  Clock clock_1 (.out(clock_1_out));
  not not_1 (not_1_out, clock_1_out);
  J_K_Flip_Flop j_k_ff_1 (
    .J(in_1), .clk(not_1_out), .K(in_1), .Q(out_6), .Qn(j_k_ff_1_qn), .en(in_2));  // open: preset, reset
  J_K_Flip_Flop j_k_ff_2 (
    .J(in_1), .clk(j_k_ff_1_qn), .K(in_1), .Q(out_5), .Qn(j_k_ff_2_qn), .en(in_2));  // open: preset, reset
  J_K_Flip_Flop j_k_ff_3 (
    .J(in_1), .clk(j_k_ff_2_qn), .K(in_1), .Q(out_4), .Qn(j_k_ff_3_qn), .en(in_2));  // open: preset, reset
  J_K_Flip_Flop j_k_ff_4 (.J(in_1), .clk(j_k_ff_3_qn), .K(in_1), .Q(out_3), .en(in_2));  // open: Qn, preset, reset

  // Notes on the sheet:
  //   MOD-16 Counter using Asynchronous Way
  //   LSB
  //   MSB
endmodule
