// Logisim project Decoder.circ as structural Verilog: 1 circuit, main circuit main
module main (
  input  in_1,
  input  [2:0] in_2,
  output out_3,
  output out_4,
  output out_5,
  output out_6,
  output out_7,
  output out_8,
  output out_9,
  output out_10
);

  Decoder #(.select(3)) decoder_1 (
    .out0(out_10), .out1(out_9), .out2(out_8), .out3(out_7), .out4(out_6), .out5(out_5), .out6(out_4),
    .out7(out_3), .sel(in_2), .en(in_1));
endmodule
