// Logisim project Mod-31 up asyn.circ as structural Verilog: 1 circuit, main circuit main
module main (
  input  in_1,
  output out_2,
  output out_3,
  output out_4,
  output out_5,
  output out_6
);

  wire and_1_out, clock_1_out, j_k_ff_1_q, j_k_ff_2_q, j_k_ff_3_q, j_k_ff_4_q;

  Clock clock_1 (.out(clock_1_out));
  J_K_Flip_Flop j_k_ff_1 (
    .J(in_1), .clk(clock_1_out), .K(in_1), .Q(j_k_ff_1_q), .Qn(out_6), .preset(and_1_out), .en(in_1));  // open: reset
  J_K_Flip_Flop j_k_ff_2 (
    .J(in_1), .clk(j_k_ff_1_q), .K(in_1), .Q(j_k_ff_2_q), .Qn(out_5), .preset(and_1_out), .en(in_1));  // open: reset
  J_K_Flip_Flop j_k_ff_3 (
    .J(in_1), .clk(j_k_ff_2_q), .K(in_1), .Q(j_k_ff_3_q), .Qn(out_4), .preset(and_1_out), .en(in_1));  // open: reset
  J_K_Flip_Flop j_k_ff_4 (
    .J(in_1), .clk(j_k_ff_3_q), .K(in_1), .Q(j_k_ff_4_q), .Qn(out_3), .preset(and_1_out), .en(in_1));  // open: reset
  and and_1 (and_1_out, out_2, out_3, out_4, out_5, out_6);
  J_K_Flip_Flop j_k_ff_5 (
    .J(in_1), .clk(j_k_ff_4_q), .K(in_1), .Qn(out_2), .preset(and_1_out), .en(in_1));  // open: Q, reset

  // Notes on the sheet:
  //   MOD-31 Up Counter Asynchronous way
endmodule
