// Logisim project Odd counter.circ as structural Verilog: 1 circuit, main circuit main
module main (
  input  in_1,
  output out_2,
  output out_3,
  output out_4
);

  wire A_qn, clock_1_out;

  Clock clock_1 (.out(clock_1_out));
  T_Flip_Flop A (.clk(clock_1_out), .T(A_qn), .Q(out_4), .Qn(A_qn), .en(in_1));  // open: preset, reset
  T_Flip_Flop B (.clk(clock_1_out), .T(out_4), .Q(out_3), .en(in_1));  // open: Qn, preset, reset
  T_Flip_Flop C (.clk(clock_1_out), .T(out_3), .Q(out_2), .en(in_1));  // open: Qn, preset, reset
endmodule
