// Logisim project Random(jk-D-jk).circ as structural Verilog: 1 circuit, main circuit main
module main (
  input  in_1,
  output out_2,
  output out_3,
  output out_4
);

  wire and_1_out, and_2_out, C_qn, clock_1_out, or_1_out;

  Clock clock_1 (.out(clock_1_out));
  J_K_Flip_Flop A (.J(in_1), .clk(clock_1_out), .K(in_1), .Q(out_4), .en(in_1));  // open: Qn, preset, reset
  or or_1 (or_1_out, out_3, out_4);
  and and_1 (and_1_out, or_1_out, C_qn);
  D_Flip_Flop B (.clk(clock_1_out), .D(and_1_out), .Q(out_3), .en(in_1));  // open: Qn, preset, reset
  and and_2 (and_2_out, out_3, out_4);
  J_K_Flip_Flop C (
    .J(and_2_out), .clk(clock_1_out), .K(out_4), .Q(out_2), .Qn(C_qn), .en(in_1));  // open: preset, reset

  // Notes on the sheet:
  //   000->001->010->011->110->101->000 Counter
endmodule
