// Logisim project even counter.circ as structural Verilog: 1 circuit, main circuit main
module main (
  input  in_1,
  output out_2,
  output out_3,
  output out_4
);

  wire clock_1_out;

  Clock clock_1 (.out(clock_1_out));
  T_Flip_Flop t_ff_1 (.clk(clock_1_out), .T(out_4), .Q(out_4), .en(in_1));  // open: Qn, preset, reset
  T_Flip_Flop t_ff_2 (.clk(clock_1_out), .T(in_1), .Q(out_3), .en(in_1));  // open: Qn, preset, reset
  T_Flip_Flop t_ff_3 (.clk(clock_1_out), .T(out_3), .Q(out_2), .en(in_1));  // open: Qn, preset, reset
endmodule
