// Logisim project exam question.circ as structural Verilog: 1 circuit, main circuit main
module main (
  input  in_1,
  output out_2,
  output out_3,
  output out_4
);

  wire and_1_out, and_2_out, clock_1_out, d_ff_1_qn, j_k_ff_1_qn, or_1_out, xnor_1_out;

  Clock clock_1 (.out(clock_1_out));
  T_Flip_Flop t_ff_1 (.clk(clock_1_out), .T(xnor_1_out), .Q(out_4), .en(in_1));  // open: Qn, preset, reset
  xnor xnor_1 (xnor_1_out, out_3, out_2);
  and and_1 (and_1_out, out_4, d_ff_1_qn);
  J_K_Flip_Flop j_k_ff_1 (
    .J(in_1), .clk(clock_1_out), .K(d_ff_1_qn), .Q(out_3), .Qn(j_k_ff_1_qn), .en(in_1));  // open: preset, reset
  and and_2 (and_2_out, j_k_ff_1_qn, out_2);
  or or_1 (or_1_out, and_2_out, and_1_out);
  D_Flip_Flop d_ff_1 (.clk(clock_1_out), .D(or_1_out), .Q(out_2), .Qn(d_ff_1_qn), .en(in_1));  // open: preset, reset
endmodule
