// Logisim project jk-d.circ as structural Verilog: 1 circuit, main circuit main
module main (
  input  in_1,
  output out_2,
  output out_3
);

  wire clock_1_out, d_ff_1_qn, not_1_out, not_2_out;

  not not_1 (not_1_out, clock_1_out);
  Clock clock_1 (.out(clock_1_out));
  J_K_Flip_Flop j_k_ff_1 (.J(in_1), .clk(not_1_out), .K(in_1), .Q(out_3), .en(in_1));  // open: Qn, preset, reset
  D_Flip_Flop d_ff_1 (.clk(not_2_out), .D(d_ff_1_qn), .Q(out_2), .Qn(d_ff_1_qn), .en(in_1));  // open: preset, reset
  not not_2 (not_2_out, out_3);
endmodule
