// Logisim project mod-64(T FF).circ as structural Verilog: 1 circuit, main circuit main
module main (
  input  in_1,
  output out_2,
  output out_3,
  output out_4,
  output out_5,
  output out_6
);

  wire clock_1_out, t_ff_1_q, t_ff_2_q, t_ff_3_q, t_ff_4_q;

  Clock clock_1 (.out(clock_1_out));
  T_Flip_Flop t_ff_1 (.clk(clock_1_out), .T(in_1), .Q(t_ff_1_q), .Qn(out_6), .en(in_1));  // open: preset, reset
  T_Flip_Flop t_ff_2 (.clk(t_ff_1_q), .T(in_1), .Q(t_ff_2_q), .Qn(out_5), .en(in_1));  // open: preset, reset
  T_Flip_Flop t_ff_3 (.clk(t_ff_2_q), .T(in_1), .Q(t_ff_3_q), .Qn(out_4), .en(in_1));  // open: preset, reset
  T_Flip_Flop t_ff_4 (.clk(t_ff_3_q), .T(in_1), .Q(t_ff_4_q), .Qn(out_3), .en(in_1));  // open: preset, reset
  T_Flip_Flop t_ff_5 (.clk(t_ff_4_q), .T(in_1), .Qn(out_2), .en(in_1));  // open: Q, preset, reset
endmodule
