// Logisim project syn_down.circ as structural Verilog: 1 circuit, main circuit main
module main (
  input  in_1,
  output out_2,
  output out_3,
  output out_4,
  output out_5
);

  wire and_1_out, and_2_out, clock_1_out, j_k_ff_2_q, j_k_ff_3_q, j_k_ff_4_q;

  J_K_Flip_Flop j_k_ff_1 (
    .J(and_1_out), .clk(clock_1_out), .K(and_1_out), .Qn(out_2), .en(in_1));  // open: Q, preset, reset
  and and_1 (and_1_out, j_k_ff_2_q, and_2_out);
  J_K_Flip_Flop j_k_ff_2 (
    .J(and_2_out), .clk(clock_1_out), .K(and_2_out), .Q(j_k_ff_2_q), .Qn(out_3), .en(in_1));  // open: preset, reset
  and and_2 (and_2_out, j_k_ff_4_q, j_k_ff_3_q);
  J_K_Flip_Flop j_k_ff_3 (
    .J(j_k_ff_4_q), .clk(clock_1_out), .K(j_k_ff_4_q), .Q(j_k_ff_3_q), .Qn(out_4), .en(in_1));  // open: preset, reset
  Clock clock_1 (.out(clock_1_out));
  J_K_Flip_Flop j_k_ff_4 (
    .J(in_1), .clk(clock_1_out), .K(in_1), .Q(j_k_ff_4_q), .Qn(out_5), .en(in_1));  // open: preset, reset

  // Notes on the sheet:
  //   Synchronous Down Counter
endmodule
