// Logisim project synchronous.circ as structural Verilog
module main (
  input  in_1,
  output out_2,
  output out_3,
  output out_4,
  output out_5
);

  wire and_1_out, and_2_out, and_3_out, clock_1_out, nor_1_out, nor_2_out, nor_3_out, not_1_out, not_2_out,
       or_1_out, or_2_out, or_3_out, or_4_out, or_5_out, or_6_out, or_7_out;

  Clock clock_1 (.out(clock_1_out));
  or or_1 (or_1_out, nor_1_out, nor_3_out);
  J_K_Flip_Flop j_k_ff_1 (
    .J(in_1), .clk(clock_1_out), .K(in_1), .Q(out_5), .en(in_1), .reset(and_2_out));  // open: Qn, preset
  nor nor_1 (nor_1_out, out_2, out_3, out_4, out_5);
  buf or_2 (or_2_out, nor_3_out);  // OR_Gate
  or or_3 (or_3_out, nor_1_out, nor_3_out);
  J_K_Flip_Flop j_k_ff_2 (
    .J(out_5), .clk(clock_1_out), .K(out_5), .Q(out_4), .en(in_1), .reset(and_2_out));  // open: Qn, preset
  not not_1 (not_1_out, out_4);
  not not_2 (not_2_out, out_5);
  nor nor_2 (nor_2_out, out_2, out_3, out_4, not_2_out);
  nor nor_3 (nor_3_out, out_2, out_3, not_1_out, out_5);
  buf or_4 (or_4_out, nor_1_out);  // OR_Gate
  _7_Segment_Display u_7_segment_display_1 (
    .g(or_2_out), .f(or_4_out), .a(or_5_out), .b(or_6_out), .e(or_3_out), .d(or_1_out), .c(or_7_out));  // open: dp
  and and_1 (and_1_out, out_5, out_4);
  and and_2 (and_2_out, out_2, out_4);
  or or_5 (or_5_out, nor_1_out, nor_3_out);
  and and_3 (and_3_out, and_1_out, out_3);
  J_K_Flip_Flop j_k_ff_3 (
    .J(and_1_out), .clk(clock_1_out), .K(and_1_out), .Q(out_3), .en(in_1), .reset(and_2_out));  // open: Qn, preset
  or or_6 (or_6_out, nor_1_out, nor_2_out, nor_3_out);
  J_K_Flip_Flop j_k_ff_4 (
    .J(and_3_out), .clk(clock_1_out), .K(and_3_out), .Q(out_2), .en(in_1), .reset(and_2_out));  // open: Qn, preset
  or or_7 (or_7_out, nor_1_out, nor_2_out);

  // Notes on the sheet:
  //   LSB
  //   MOD-10 Calculation Using Synchronous way
  //   MSB
endmodule
