// Logisim project NAND_NOR_with_NMOS.circ as structural Verilog: 1 circuit, main circuit main
module main (
  input  in_1,
  input  in_2,
  input  in_3,
  input  in_4,
  output out_5,
  output out_6
);

  wire transistor_2_out;

  Pull_Resistor #(.pull(1)) pull_resistor_1 (.node(out_5));
  Transistor #(.\type ("n")) transistor_1 (.in(transistor_2_out), .out(out_5), .gate(in_1));
  Transistor #(.\type ("n")) transistor_2 (.in(1'b0), .out(transistor_2_out), .gate(in_2));
  Pull_Resistor #(.pull(1)) pull_resistor_2 (.node(out_6));
  Transistor #(.\type ("n")) transistor_3 (.in(1'b0), .out(out_6), .gate(in_3));
  Transistor #(.\type ("n")) transistor_4 (.in(1'b0), .out(out_6), .gate(in_4));

  // Notes on the sheet:
  //   NAND Gate
  //   NOR Gate
endmodule
