// Logisim project Full_Adder.circ as structural Verilog: 2 circuits, main circuit main
module main (
  input  A,
  input  B,
  input  C,
  output Sum,
  output Carry
);

  wire and_1_out, and_2_out, xor_1_out;

  xor xor_1 (xor_1_out, A, B);
  xor xor_2 (Sum, xor_1_out, C);
  and and_1 (and_1_out, C, xor_1_out);
  and and_2 (and_2_out, A, B);
  or or_1 (Carry, and_1_out, and_2_out);
endmodule

module FA4 (
  input  [3:0] in_1,
  input  [3:0] in_2,
  input  in_3
);

  wire main_1_p1, main_1_p2, main_2_p1, main_2_p5, main_3_p3, main_3_p4;

  // Probe on main_1_p1
  // main main_1: pin names not known; wires that end beside it: main_1_p1, main_1_p2, in_1[3], in_1[2]
  // Probe on main_1_p2
  // main main_2: pin names not known; wires that end beside it: main_2_p1, in_1[3], in_1[3], main_2_p1, main_2_p5, in_1[2]
  // Probe on main_2_p5
  // main main_3: pin names not known; wires that end beside it: in_1[2], in_1[2], main_3_p3, main_3_p4, main_3_p4, in_1[2], in_2[2]
  // Probe on main_3_p3
  // Probe on nothing
  // main main_4: pin names not known; wires that end beside it: in_1[2], in_1[1], in_2[3], in_2[1], in_1[0], in_2[0]
  // Probe on nothing
endmodule
