// Logisim project ALU_Library.circ as structural Verilog
module OR_Gate (
  input  [3:0] in_1,
  input  [3:0] in_2
);

  wire Q0, Q1, Q2, Q3;

  or or_1 (Q0, in_1[0], in_2[0]);
  or or_2 (Q1, in_1[1], in_2[1]);
  or or_3 (Q2, in_1[2], in_2[2]);
  or or_4 (Q3, in_1[3], in_2[3]);
  // Probe on {Q3, Q2, Q1, Q0}

  // Other names for the same wires on the sheet: A0 = in_1[0]; A1 = in_1[1]; A2 = in_1[2]; A3 = in_1[3]; B0 = in_2[0];
  //   B1 = in_2[1]; B2 = in_2[2]; B3 = in_2[3]
endmodule

module AND_gate (
  input  [3:0] in_1,
  input  [3:0] in_2
);

  wire Q0, Q1, Q2, Q3;

  and and_1 (Q0, in_1[0], in_2[0]);
  and and_2 (Q1, in_1[1], in_2[1]);
  and and_3 (Q2, in_1[2], in_2[2]);
  and and_4 (Q3, in_1[3], in_2[3]);
  // Probe on {Q3, Q2, Q1, Q0}

  // Other names for the same wires on the sheet: A0 = in_1[0]; A1 = in_1[1]; A2 = in_1[2]; A3 = in_1[3]; B0 = in_2[0];
  //   B1 = in_2[1]; B2 = in_2[2]; B3 = in_2[3]
endmodule

module XOR_gate (
  input  [3:0] in_1,
  input  [3:0] in_2
);

  wire Q0, Q1, Q2, Q3;

  xor xor_1 (Q0, in_1[0], in_2[0]);
  xor xor_2 (Q1, in_1[1], in_2[1]);
  xor xor_3 (Q2, in_1[2], in_2[2]);
  xor xor_4 (Q3, in_1[3], in_2[3]);
  // Probe on {Q3, Q2, Q1, Q0}

  // Other names for the same wires on the sheet: A0 = in_1[0]; A1 = in_1[1]; A2 = in_1[2]; A3 = in_1[3]; B0 = in_2[0];
  //   B1 = in_2[1]; B2 = in_2[2]; B3 = in_2[3]
endmodule

module NOT_gate (
  input  [3:0] in_1
);

  wire Q0, Q1, Q2, Q3;

  not not_1 (Q0, in_1[0]);
  not not_2 (Q1, in_1[1]);
  not not_3 (Q2, in_1[2]);
  not not_4 (Q3, in_1[3]);
  // Probe on {Q3, Q2, Q1, Q0}

  // Other names for the same wires on the sheet: A0 = in_1[0]; A1 = in_1[1]; A2 = in_1[2]; A3 = in_1[3]
endmodule

module Left_shift (
  input  in_1,
  input  [3:0] A,
  input  [1:0] Shift
);

  wire F0, F1, F2, F3;

  // Probe on {F3, F2, F1, F0}
  Multiplexer #(.select(2)) multiplexer_1 (.in0(A[3]), .in1(A[2]), .in2(A[1]), .in3(A[0]), .out(F3), .sel(Shift));
  Multiplexer #(.select(2)) multiplexer_2 (.in0(A[2]), .in1(A[1]), .in2(A[0]), .in3(in_1), .out(F2), .sel(Shift));
  Multiplexer #(.select(2)) multiplexer_3 (.in0(A[1]), .in1(A[0]), .in2(in_1), .in3(in_1), .out(F1), .sel(Shift));
  Multiplexer #(.select(2)) multiplexer_4 (.in0(A[0]), .in1(in_1), .in2(in_1), .in3(in_1), .out(F0), .sel(Shift));
endmodule

module Right_shift (
  input  in_1,
  input  [3:0] A,
  input  [1:0] Shift
);

  wire F0, F1, F2, F3;

  // Probe on {F3, F2, F1, F0}
  Multiplexer #(.select(2)) multiplexer_1 (.in0(A[3]), .in1(in_1), .in2(in_1), .in3(in_1), .out(F3), .sel(Shift));
  Multiplexer #(.select(2)) multiplexer_2 (.in0(A[2]), .in1(A[3]), .in2(in_1), .in3(in_1), .out(F2), .sel(Shift));
  Multiplexer #(.select(2)) multiplexer_3 (.in0(A[1]), .in1(A[2]), .in2(A[3]), .in3(in_1), .out(F1), .sel(Shift));
  Multiplexer #(.select(2)) multiplexer_4 (.in0(A[0]), .in1(A[1]), .in2(A[2]), .in3(A[3]), .out(F0), .sel(Shift));
endmodule

module ASR (
  input  in_1,
  input  [3:0] A,
  input  [1:0] Shift
);

  wire F0, F1, F2, F3;

  // Probe on {F3, F2, F1, F0}
  Multiplexer #(.select(2)) multiplexer_1 (.in0(A[3]), .in1(A[3]), .in2(A[3]), .in3(A[3]), .out(F3), .sel(Shift));
  Multiplexer #(.select(2)) multiplexer_2 (.in0(A[2]), .in1(A[3]), .in2(A[3]), .in3(A[3]), .out(F2), .sel(Shift));
  Multiplexer #(.select(2)) multiplexer_3 (.in0(A[1]), .in1(A[2]), .in2(A[3]), .in3(A[3]), .out(F1), .sel(Shift));
  Multiplexer #(.select(2)) multiplexer_4 (.in0(A[0]), .in1(A[1]), .in2(A[2]), .in3(A[3]), .out(F0), .sel(Shift));
endmodule

module FA1_bit (
  input  A,
  input  B,
  input  CIN,
  output S,
  output C
);

  wire and_1_out, and_2_out, and_3_out, xor_1_out;

  and and_1 (and_1_out, A, B);
  and and_2 (and_2_out, B, CIN);
  and and_3 (and_3_out, A, CIN);
  xor xor_1 (xor_1_out, A, B);
  xor xor_2 (S, xor_1_out, CIN);
  or or_1 (C, and_1_out, and_2_out, and_3_out);
endmodule

module FA_4BIT (
  input  [3:0] in_1,
  input  [3:0] A,
  input  in_3
);

  wire fa1_bit_1_c, fa1_bit_1_s, fa1_bit_2_c, fa1_bit_2_s, fa1_bit_3_c, fa1_bit_3_s, fa1_bit_4_c,
       fa1_bit_4_s, xor_1_out, xor_2_out, xor_3_out, xor_4_out;

  FA1_bit fa1_bit_1 (.B(xor_1_out), .CIN(fa1_bit_2_c), .A(A[3]), .C(fa1_bit_1_c), .S(fa1_bit_1_s));
  xor xor_1 (xor_1_out, in_1[3], in_3);
  FA1_bit fa1_bit_2 (.B(xor_2_out), .CIN(fa1_bit_3_c), .A(A[2]), .C(fa1_bit_2_c), .S(fa1_bit_2_s));
  xor xor_2 (xor_2_out, in_1[2], in_3);
  FA1_bit fa1_bit_3 (.B(xor_3_out), .CIN(fa1_bit_4_c), .A(A[1]), .C(fa1_bit_3_c), .S(fa1_bit_3_s));
  // Probe on fa1_bit_1_c
  // Probe on fa1_bit_1_s
  xor xor_3 (xor_3_out, in_1[1], in_3);
  // Probe on fa1_bit_2_s
  FA1_bit fa1_bit_4 (.B(xor_4_out), .CIN(in_3), .A(A[0]), .C(fa1_bit_4_c), .S(fa1_bit_4_s));
  // Probe on fa1_bit_3_s
  // Probe on fa1_bit_4_s
  xor xor_4 (xor_4_out, in_1[0], in_3);
endmodule

module MUL2_2 (
  input  in_1,
  input  in_2,
  input  in_3,
  input  in_4,
  output out_5,
  output out_6,
  output out_7
);

  wire and_1_out;

  FA1_bit fa1_bit_1 (.B(and_1_out), .CIN(in_4), .A(in_3), .C(out_6), .S(out_7));
  and and_1 (and_1_out, in_2, in_1);

  assign out_5 = in_2;
endmodule

module Full_MUL (
  input  [1:0] in_1,
  input  [1:0] y,
  input  in_3
);

  wire mul2_2_1_out_6, mul2_2_1_out_7, mul2_2_2_out_5, mul2_2_2_out_6, mul2_2_2_out_7, mul2_2_3_out_6,
       mul2_2_3_out_7, mul2_2_4_out_5, mul2_2_4_out_6, mul2_2_4_out_7;

  MUL2_2 mul2_2_1 (
    .in_1(y[1]), .in_4(mul2_2_3_out_6), .in_3(mul2_2_2_out_6), .in_2(mul2_2_2_out_5), .out_6(mul2_2_1_out_6),
    .out_7(mul2_2_1_out_7));  // open: out_5
  // Probe on mul2_2_1_out_6
  // Probe on mul2_2_1_out_7
  // Probe on mul2_2_3_out_7
  // Probe on mul2_2_4_out_7
  MUL2_2 mul2_2_2 (
    .in_1(y[0]), .in_4(mul2_2_4_out_6), .in_3(in_3), .in_2(in_1[1]), .out_5(mul2_2_2_out_5),
    .out_6(mul2_2_2_out_6), .out_7(mul2_2_2_out_7));
  MUL2_2 mul2_2_3 (
    .in_1(y[1]), .in_4(in_3), .in_3(mul2_2_2_out_7), .in_2(mul2_2_4_out_5), .out_6(mul2_2_3_out_6),
    .out_7(mul2_2_3_out_7));  // open: out_5
  MUL2_2 mul2_2_4 (
    .in_1(y[0]), .in_4(in_3), .in_3(in_3), .in_2(in_1[0]), .out_5(mul2_2_4_out_5), .out_6(mul2_2_4_out_6),
    .out_7(mul2_2_4_out_7));
endmodule
