// Logisim project circuit.circ as structural Verilog
module ASR (
  input  [1:0] in_1,
  input  [3:0] A
);

  wire F0, F1, F2, F3;

  Multiplexer #(.select(2)) multiplexer_1 (.in0(A[3]), .in1(A[3]), .in2(A[3]), .in3(A[3]), .out(F3), .sel(in_1));
  Multiplexer #(.select(2)) multiplexer_2 (.in0(A[2]), .in1(A[3]), .in2(A[3]), .in3(A[3]), .out(F2), .sel(in_1));
  // Probe on {F3, F2, F1, F0}
  Multiplexer #(.select(2)) multiplexer_3 (.in0(A[1]), .in1(A[2]), .in2(A[3]), .in3(A[3]), .out(F1), .sel(in_1));
  Multiplexer #(.select(2)) multiplexer_4 (.in0(A[0]), .in1(A[1]), .in2(A[2]), .in3(A[3]), .out(F0), .sel(in_1));
endmodule

module single_bit_subtractor (
  input  A,
  input  B,
  input  Bin,
  output D,
  output Bout
);

  wire and_1_out, and_2_out, not_1_out, not_2_out, xor_1_out;

  xor xor_1 (xor_1_out, A, B);
  not not_1 (not_1_out, xor_1_out);
  not not_2 (not_2_out, A);
  xor xor_2 (D, xor_1_out, Bin);
  and and_1 (and_1_out, not_1_out, Bin);
  and and_2 (and_2_out, B, not_2_out);
  or or_1 (Bout, and_1_out, and_2_out);
endmodule

module Full_Subtractor (
  input  [3:0] A,
  input  [3:0] B,
  input  Bin
);

  wire Bout, D0, D1, D2, D3, single_bit_subtractor_2_bout, single_bit_subtractor_3_bout,
       single_bit_subtractor_4_bout;

  single_bit_subtractor single_bit_subtractor_1 (
    .A(A[3]), .B(B[3]), .Bin(single_bit_subtractor_2_bout), .D(D3), .Bout(Bout));
  single_bit_subtractor single_bit_subtractor_2 (
    .A(A[2]), .B(B[2]), .Bin(single_bit_subtractor_3_bout), .D(D2), .Bout(single_bit_subtractor_2_bout));
  // Probe on Bout
  single_bit_subtractor single_bit_subtractor_3 (
    .A(A[1]), .B(B[1]), .Bin(single_bit_subtractor_4_bout), .D(D1), .Bout(single_bit_subtractor_3_bout));
  // Probe on {D3, D2, D1, D0}
  single_bit_subtractor single_bit_subtractor_4 (
    .A(A[0]), .B(B[0]), .Bin(Bin), .D(D0), .Bout(single_bit_subtractor_4_bout));
endmodule

module Right_shift (
  input  in_1,
  input  [1:0] in_2,
  input  [3:0] A
);

  wire F0, F1, F2, F3;

  Multiplexer #(.select(2)) multiplexer_1 (.in0(A[3]), .in1(in_1), .in2(in_1), .in3(in_1), .out(F3), .sel(in_2));
  Multiplexer #(.select(2)) multiplexer_2 (.in0(A[2]), .in1(A[3]), .in2(in_1), .in3(in_1), .out(F2), .sel(in_2));
  // Probe on {F3, F2, F1, F0}
  Multiplexer #(.select(2)) multiplexer_3 (.in0(A[1]), .in1(A[2]), .in2(A[3]), .in3(in_1), .out(F1), .sel(in_2));
  Multiplexer #(.select(2)) multiplexer_4 (.in0(A[0]), .in1(A[1]), .in2(A[2]), .in3(A[3]), .out(F0), .sel(in_2));
endmodule

module CMOS_Design (
  input  [3:0] ABCD,
  output F
);

  wire transistor_1_out, transistor_4_out, transistor_8_out;

  Transistor transistor_1 (.in(1'b1), .out(transistor_1_out), .gate(ABCD[3]));
  Transistor transistor_2 (.in(transistor_1_out), .out(F), .gate(ABCD[1]));
  Transistor #(.\type ("n")) transistor_3 (.in(transistor_4_out), .out(F), .gate(ABCD[3]));
  Transistor #(.\type ("n")) transistor_4 (.in(1'b0), .out(transistor_4_out), .gate(ABCD[2]));
  Transistor transistor_5 (.in(1'b1), .out(transistor_1_out), .gate(ABCD[2]));
  Transistor transistor_6 (.in(transistor_1_out), .out(F), .gate(ABCD[0]));
  Transistor #(.\type ("n")) transistor_7 (.in(transistor_8_out), .out(F), .gate(ABCD[1]));
  Transistor #(.\type ("n")) transistor_8 (.in(1'b0), .out(transistor_8_out), .gate(ABCD[0]));

  // Other names for the same wires on the sheet: D = ABCD[0]; C = ABCD[1]; B = ABCD[2]; A = ABCD[3]
endmodule

module NMOS_circuit (
  input  [3:0] ABCD,
  output out_2
);

  wire transistor_3_out, transistor_4_out;

  Pull_Resistor #(.pull(1)) pull_resistor_1 (.node(out_2));
  Transistor #(.\type ("n")) transistor_1 (.in(transistor_3_out), .out(out_2), .gate(ABCD[3]));
  Transistor #(.\type ("n")) transistor_2 (.in(transistor_4_out), .out(out_2), .gate(ABCD[1]));
  Transistor #(.\type ("n")) transistor_3 (.in(1'b0), .out(transistor_3_out), .gate(ABCD[2]));
  Transistor #(.\type ("n")) transistor_4 (.in(1'b0), .out(transistor_4_out), .gate(ABCD[0]));

  // Other names for the same wires on the sheet: D = ABCD[0]; C = ABCD[1]; B = ABCD[2]; A = ABCD[3]
endmodule

module Left_shift (
  input  in_1,
  input  [1:0] in_2,
  input  [3:0] A
);

  wire F0, F1, F2, F3;

  Multiplexer #(.select(2)) multiplexer_1 (.in0(A[3]), .in1(A[2]), .in2(A[1]), .in3(A[0]), .out(F3), .sel(in_2));
  Multiplexer #(.select(2)) multiplexer_2 (.in0(A[2]), .in1(A[1]), .in2(A[0]), .in3(in_1), .out(F2), .sel(in_2));
  // Probe on {F3, F2, F1, F0}
  Multiplexer #(.select(2)) multiplexer_3 (.in0(A[1]), .in1(A[0]), .in2(in_1), .in3(in_1), .out(F1), .sel(in_2));
  Multiplexer #(.select(2)) multiplexer_4 (.in0(A[0]), .in1(in_1), .in2(in_1), .in3(in_1), .out(F0), .sel(in_2));
endmodule
